# Fritzing sketch xbee-assignment-1 (saved by Fritzing 0.9.2b)
breadboards: 1

parts:
  Part1 = Arduino Uno (Rev3)
  R1 = Resistor [tolerance=±5% resistance=10k package=THT]
  LED1 = LED - 5mm [color="Green (565nm)" package="5 mm [THT]"]  # not connected
  R2 = Resistor [tolerance=±5% resistance=10k package=THT]
  LED2 = LED - 5mm [color="Red (633nm)" package="5 mm [THT]"]  # not connected
  R3 = Resistor [tolerance=±10% resistance=10k package=THT]
  S1 = Pushbutton [package="[THT]"]
  R5 = TRIMPOT [package=3362u-2]
  xbee1 = Adafruit Xbee Adapter v1.1 [part_number=126]
  U1 = XBEE-1 [package=xbee-silk]

nets:
  N1: Part1.A0, R5.WIPER
  N2: Part1.D8, R3.Pin_1, S1.Pin_3, S1.Pin_4
  N3: Part1.D2, xbee1.tx
  N4: Part1.D3_PWM, xbee1.rx
  N5: Part1.D5_PWM, R1.Pin_1
  N6: Part1.D6_PWM, R2.Pin_1
  5V: Part1.5V, R3.Pin_0, R5.CW, xbee1.+5v
  GND: Part1.GND, S1.Pin_1, S1.Pin_2, R5.CCW, xbee1.gnd
  N7: xbee1.3v#1, U1.GND
  N8: xbee1.3v#10, U1.DIO4
  N9: U1.RESET, U1.RTS
  N10: U1.RSSI, U1.DIO5

custom parts:
  Adafruit Xbee Adapter v1.1: Adafruit Xbee Adapter
